// Logisim project 8BitBenEater.circ as structural Verilog: 4 circuits, main circuit main
module main (
  input  in_1,
  input  in_2,
  input  in_3
);

  wire clk_1_clk_out, clock_1_out;
  wire [3:0] pull_resistor_8_node;
  wire [7:4] pull_resistor_4_node;

  Clock clock_1 (.out(clock_1_out));
  CLK clk_1 (.CLK_IN(clock_1_out), .CLK_ENB(in_1), .CLK_MANUAL(in_2), .HALT(in_3), .CLK_OUT(clk_1_clk_out));
  LED led_1 (.in(pull_resistor_4_node[7]));
  LED led_2 (.in(pull_resistor_4_node[6]));
  LED led_3 (.in(pull_resistor_4_node[5]));
  LED led_4 (.in(pull_resistor_4_node[4]));
  Pull_Resistor pull_resistor_1 (.node(pull_resistor_4_node[7]));
  Pull_Resistor pull_resistor_2 (.node(pull_resistor_4_node[6]));
  Pull_Resistor pull_resistor_3 (.node(pull_resistor_4_node[5]));
  Pull_Resistor pull_resistor_4 (.node(pull_resistor_4_node[4]));
  LED led_5 (.in(pull_resistor_8_node[3]));
  LED led_6 (.in(pull_resistor_8_node[2]));
  LED led_7 (.in(pull_resistor_8_node[1]));
  LED led_8 (.in(pull_resistor_8_node[0]));
  Pull_Resistor pull_resistor_5 (.node(pull_resistor_8_node[3]));
  Pull_Resistor pull_resistor_6 (.node(pull_resistor_8_node[2]));
  Pull_Resistor pull_resistor_7 (.node(pull_resistor_8_node[1]));
  Pull_Resistor pull_resistor_8 (.node(pull_resistor_8_node[0]));
  PROGRAM_COUNTER program_counter_1 (
    .CLOCK(clk_1_clk_out), .ADDRESS_IN(pull_resistor_8_node), .ADDRESS_OUT(pull_resistor_8_node));  // open: RESET, JUMP, COUNTER_ENABLE, COUNTER_OUT, ALWAYS_OUT
  REGISTER_A register_a_1 (
    .DATA_IN({pull_resistor_4_node, pull_resistor_8_node}), .CLOCK(clk_1_clk_out),
    .DATA_OUT({pull_resistor_4_node, pull_resistor_8_node}));  // open: A_IN, A_OUT, A_RESET, ALWAYS_OUT
endmodule

module CLK (
  input  CLK_IN,
  input  CLK_ENB,
  input  CLK_MANUAL,
  input  HALT,
  output CLK_OUT
);

  wire and_1_out, and_2_out, not_1_out, not_2_out, or_1_out;

  not not_1 (not_1_out, CLK_ENB);
  not not_2 (not_2_out, HALT);
  and and_1 (and_1_out, CLK_IN, CLK_ENB);
  and and_2 (and_2_out, not_1_out, CLK_MANUAL);
  or or_1 (or_1_out, and_1_out, and_2_out);
  and and_3 (CLK_OUT, or_1_out, not_2_out);
endmodule

module PROGRAM_COUNTER (
  input  RESET,
  input  JUMP,
  input  COUNTER_ENABLE,
  input  CLOCK,
  input  [3:0] ADDRESS_IN,
  input  COUNTER_OUT,
  output [3:0] ALWAYS_OUT,
  output [3:0] ADDRESS_OUT
);

  Counter #(.max('hf), .width(4)) counter_1 (
    .clr(RESET), .load(JUMP), .up(COUNTER_ENABLE), .count(COUNTER_ENABLE), .clk(CLOCK), .D(ADDRESS_IN),
    .Q(ALWAYS_OUT));  // open: carry
  assign ADDRESS_OUT = COUNTER_OUT ? ALWAYS_OUT : 4'bz;  // Controlled_Buffer controlled_buffer_1
endmodule

module REGISTER_A (
  input  [7:0] DATA_IN,
  input  A_IN,
  input  A_OUT,
  input  CLOCK,
  input  A_RESET,
  output [7:0] ALWAYS_OUT,
  output [7:0] DATA_OUT
);

  Register register_1 (.D(DATA_IN), .en(A_IN), .clk(CLOCK), .Q(ALWAYS_OUT), .clr(A_RESET));
  assign DATA_OUT = A_OUT ? ALWAYS_OUT : 8'bz;  // Controlled_Buffer controlled_buffer_1
endmodule
